// Digital circuit overture.dig as structural Verilog
module overture (
);

  wire and_1_out, and_2_out, and_3_out, and_4_out, and_5_out, and_6_out, and_7_out, and_8_out, and_9_out,
       and_10_out, and_11_out, and_12_out, and_13_out, and_14_out, and_15_out, and_16_out, and_17_out,
       and_18_out, and_19_out, and_20_out, and_21_out, and_22_out, and_23_out, and_24_out, and_25_out,
       and_26_out, and_27_out, and_28_out, and_29_out, and_30_out, and_31_out, and_32_out, and_33_out,
       and_34_out, and_35_out, and_36_out, and_37_out, and_38_out, and_39_out, and_40_out, and_41_out,
       and_42_out, and_43_out, and_44_out, and_45_out, and_46_out, and_47_out, and_49_out, and_50_out,
       and_51_out, and_52_out, and_53_out, and_54_out, and_55_out, and_56_out, and_57_out, and_58_out,
       and_59_out, and_60_out, and_61_out, and_62_out, and_63_out, and_64_out, and_65_out, and_66_out,
       and_67_out, and_68_out, and_69_out, and_70_out, and_71_out, and_72_out, and_73_out, and_74_out,
       and_75_out, and_76_out, and_77_out, and_78_out, and_79_out, and_80_out, and_81_out, and_82_out,
       and_83_out, dipswitch_1_out, dipswitch_2_out, dipswitch_3_out, nand_1_out, nand_2_out, nand_3_out,
       nand_4_out, nand_5_out, nand_6_out, nand_7_out, nand_8_out, nor_1_out, nor_2_out, nor_3_out,
       nor_4_out, nor_5_out, nor_6_out, nor_7_out, nor_8_out, nor_9_out, nor_10_out, nor_11_out, nor_12_out,
       nor_13_out, nor_14_out, nor_15_out, nor_16_out, nor_17_out, nor_18_out, nor_19_out, nor_20_out,
       nor_21_out, nor_22_out, nor_23_out, nor_24_out, nor_25_out, nor_26_out, not_1_out, not_2_out,
       not_3_out, not_4_out, not_5_out, not_6_out, not_7_out, not_8_out, not_9_out, not_10_out, not_11_out,
       not_12_out, not_13_out, not_14_out, not_15_out, not_16_out, not_17_out, notconnected_1_out,
       notconnected_2_out, notconnected_6_out, notconnected_11_out, notconnected_15_out, or_1_out, or_2_out,
       or_3_out, or_4_out, or_5_out, or_6_out, or_7_out, or_8_out, or_9_out, or_10_out, or_11_out, or_12_out,
       or_13_out, or_14_out, or_15_out, or_16_out, undriven, undriven_2, undriven_3, xor_1_out, xor_2_out,
       xor_3_out, xor_4_out, xor_5_out, xor_6_out, xor_7_out, xor_8_out, xor_9_out, xor_10_out, xor_11_out,
       xor_12_out, xor_13_out, xor_14_out, xor_15_out, xor_16_out, xor_17_out, xor_18_out, xor_19_out,
       xor_20_out, xor_21_out, xor_22_out, xor_23_out, xor_24_out, xor_25_out, xor_26_out, xor_27_out,
       xor_28_out, xor_29_out, xor_30_out, xor_31_out, xor_32_out;
  wire [7:0] notconnected_3_out, notconnected_4_out, notconnected_5_out, notconnected_7_out,
       notconnected_8_out, notconnected_9_out, notconnected_10_out, notconnected_12_out, notconnected_13_out,
       notconnected_14_out;

  // NotConnected on notconnected_1_out
  // NotConnected on notconnected_2_out
  // NotConnected on notconnected_3_out
  // NotConnected on notconnected_4_out
  // NotConnected on notconnected_5_out
  DipSwitch dipswitch_1 (.out(dipswitch_1_out));
  DipSwitch dipswitch_2 (.out(dipswitch_2_out));
  DipSwitch dipswitch_3 (.out(dipswitch_3_out));
  not not_1 (not_1_out, notconnected_3_out[7]);
  and and_1 (and_1_out, notconnected_1_out, notconnected_3_out[7]);
  not not_2 (not_2_out, notconnected_3_out[6]);
  and and_2 (and_2_out, notconnected_1_out, notconnected_3_out[6]);
  not not_3 (not_3_out, notconnected_3_out[5]);
  and and_3 (and_3_out, notconnected_1_out, notconnected_3_out[5]);
  not not_4 (not_4_out, notconnected_3_out[4]);
  and and_4 (and_4_out, notconnected_1_out, notconnected_3_out[4]);
  not not_5 (not_5_out, notconnected_3_out[3]);
  and and_5 (and_5_out, notconnected_1_out, notconnected_3_out[3]);
  not not_6 (not_6_out, notconnected_3_out[2]);
  and and_6 (and_6_out, notconnected_1_out, notconnected_3_out[2]);
  not not_7 (not_7_out, notconnected_3_out[1]);
  and and_7 (and_7_out, notconnected_1_out, notconnected_3_out[1]);
  not not_8 (not_8_out, notconnected_3_out[0]);
  and and_8 (and_8_out, notconnected_1_out, notconnected_3_out[0]);
  and and_9 (and_9_out, not_9_out, dipswitch_2_out);
  not not_9 (not_9_out, dipswitch_3_out);
  and and_10 (and_10_out, dipswitch_2_out, dipswitch_3_out);
  and and_11 (and_11_out, not_1_out, notconnected_1_out);
  and and_12 (and_12_out, not_2_out, notconnected_1_out);
  and and_13 (and_13_out, not_3_out, notconnected_1_out);
  and and_14 (and_14_out, not_4_out, notconnected_1_out);
  and and_15 (and_15_out, not_5_out, notconnected_1_out);
  and and_16 (and_16_out, not_6_out, notconnected_1_out);
  and and_17 (and_17_out, not_7_out, notconnected_1_out);
  and and_18 (and_18_out, not_8_out, notconnected_1_out);
  nor nor_1 (nor_1_out, and_11_out, nor_2_out);
  nor nor_2 (nor_2_out, nor_1_out, and_1_out);
  nor nor_3 (nor_3_out, and_12_out, nor_4_out);
  nor nor_4 (nor_4_out, nor_3_out, and_2_out);
  nor nor_5 (nor_5_out, and_13_out, nor_6_out);
  nor nor_6 (nor_6_out, nor_5_out, and_3_out);
  nor nor_7 (nor_7_out, and_14_out, nor_8_out);
  nor nor_8 (nor_8_out, nor_7_out, and_4_out);
  nor nor_9 (nor_9_out, and_15_out, nor_10_out);
  nor nor_10 (nor_10_out, nor_9_out, and_5_out);
  nor nor_11 (nor_11_out, and_16_out, nor_12_out);
  nor nor_12 (nor_12_out, nor_11_out, and_6_out);
  nor nor_13 (nor_13_out, and_17_out, nor_14_out);
  nor nor_14 (nor_14_out, nor_13_out, and_7_out);
  nor nor_15 (nor_15_out, and_18_out, nor_16_out);
  nor nor_16 (nor_16_out, nor_15_out, and_8_out);
  and and_19 (and_19_out, notconnected_4_out[7], notconnected_5_out[7]);
  xor xor_1 (xor_1_out, notconnected_5_out[7], notconnected_4_out[7]);
  and and_20 (and_20_out, notconnected_4_out[6], notconnected_5_out[6]);
  xor xor_2 (xor_2_out, notconnected_5_out[6], notconnected_4_out[6]);
  and and_21 (and_21_out, notconnected_4_out[5], notconnected_5_out[5]);
  xor xor_3 (xor_3_out, notconnected_5_out[5], notconnected_4_out[5]);
  and and_22 (and_22_out, notconnected_4_out[4], notconnected_5_out[4]);
  xor xor_4 (xor_4_out, notconnected_5_out[4], notconnected_4_out[4]);
  and and_23 (and_23_out, notconnected_4_out[3], notconnected_5_out[3]);
  xor xor_5 (xor_5_out, notconnected_5_out[3], notconnected_4_out[3]);
  and and_24 (and_24_out, notconnected_4_out[2], notconnected_5_out[2]);
  xor xor_6 (xor_6_out, notconnected_5_out[2], notconnected_4_out[2]);
  and and_25 (and_25_out, notconnected_4_out[1], notconnected_5_out[1]);
  xor xor_7 (xor_7_out, notconnected_5_out[1], notconnected_4_out[1]);
  and and_26 (and_26_out, notconnected_4_out[0], notconnected_5_out[0]);
  xor xor_8 (xor_8_out, notconnected_5_out[0], notconnected_4_out[0]);
  nor nor_17 (nor_17_out, and_9_out, nor_18_out);
  nor nor_18 (nor_18_out, nor_17_out, and_10_out);
  or or_1 (or_1_out, and_19_out, and_27_out);
  and and_27 (and_27_out, xor_1_out, or_2_out);
  xor xor_9 (xor_9_out, xor_1_out, or_2_out);
  or or_2 (or_2_out, and_20_out, and_28_out);
  and and_28 (and_28_out, xor_2_out, or_3_out);
  xor xor_10 (xor_10_out, xor_2_out, or_3_out);
  or or_3 (or_3_out, and_21_out, and_29_out);
  and and_29 (and_29_out, xor_3_out, or_4_out);
  xor xor_11 (xor_11_out, xor_3_out, or_4_out);
  or or_4 (or_4_out, and_22_out, and_30_out);
  and and_30 (and_30_out, xor_4_out, or_5_out);
  xor xor_12 (xor_12_out, xor_4_out, or_5_out);
  or or_5 (or_5_out, and_23_out, and_39_out);
  or or_6 (or_6_out, and_24_out, and_40_out);
  or or_7 (or_7_out, and_25_out, and_41_out);
  or or_8 (or_8_out, and_26_out, and_42_out);
  // NotConnected on notconnected_6_out
  Reset reset_1 ();  // open: out
  Reset reset_2 ();  // open: out
  and and_31 (and_31_out, nor_1_out, notconnected_2_out);
  Reset reset_3 ();  // open: out
  and and_32 (and_32_out, nor_3_out, notconnected_2_out);
  Reset reset_4 ();  // open: out
  and and_33 (and_33_out, nor_5_out, notconnected_2_out);
  Reset reset_5 ();  // open: out
  and and_34 (and_34_out, nor_7_out, notconnected_2_out);
  Reset reset_6 ();  // open: out
  and and_35 (and_35_out, nor_9_out, notconnected_2_out);
  Reset reset_7 ();  // open: out
  and and_36 (and_36_out, nor_11_out, notconnected_2_out);
  Reset reset_8 ();  // open: out
  and and_37 (and_37_out, nor_13_out, notconnected_2_out);
  Reset reset_9 ();  // open: out
  and and_38 (and_38_out, nor_15_out, notconnected_2_out);
  and and_39 (and_39_out, xor_5_out, or_6_out);
  xor xor_13 (xor_13_out, xor_5_out, or_6_out);
  and and_40 (and_40_out, xor_6_out, or_7_out);
  xor xor_14 (xor_14_out, xor_6_out, or_7_out);
  and and_41 (and_41_out, xor_7_out, or_8_out);
  xor xor_15 (xor_15_out, xor_7_out, or_8_out);
  and and_42 (and_42_out, xor_8_out, notconnected_6_out);
  xor xor_16 (xor_16_out, xor_8_out, notconnected_6_out);
  and and_43 (and_43_out, nor_17_out, dipswitch_1_out);
  // NotConnected on notconnected_7_out
  // NotConnected on notconnected_8_out
  // NotConnected on notconnected_9_out
  // NotConnected on notconnected_10_out
  and and_44 (and_44_out, notconnected_8_out[0], notconnected_8_out[0]);
  or or_9 (or_9_out, notconnected_9_out[0], notconnected_9_out[0]);
  xor xor_17 (xor_17_out, notconnected_10_out[0], notconnected_10_out[0]);
  and and_45 (and_45_out, notconnected_8_out[1], notconnected_8_out[1]);
  or or_10 (or_10_out, notconnected_9_out[1], notconnected_9_out[1]);
  xor xor_18 (xor_18_out, notconnected_10_out[1], notconnected_10_out[1]);
  not not_10 (not_10_out, notconnected_11_out);
  // NotConnected on notconnected_11_out
  and and_46 (and_46_out, notconnected_8_out[2], notconnected_8_out[2]);
  and and_47 (and_47_out, notconnected_8_out[3], notconnected_8_out[3]);
  or or_11 (or_11_out, notconnected_9_out[2], notconnected_9_out[2]);
  or or_12 (or_12_out, notconnected_9_out[3], notconnected_9_out[3]);
  xor xor_19 (xor_19_out, notconnected_10_out[2], notconnected_10_out[2]);
  xor xor_20 (xor_20_out, notconnected_10_out[3], notconnected_10_out[3]);
  // And and_48 has open pins: In_1=and_49_out, In_2=notconnected_7_out[7], out=open
  xor xor_21 (xor_21_out, notconnected_7_out[7], and_49_out);
  and and_49 (and_49_out, and_50_out, notconnected_7_out[6]);
  xor xor_22 (xor_22_out, notconnected_7_out[6], and_50_out);
  and and_50 (and_50_out, and_51_out, notconnected_7_out[5]);
  xor xor_23 (xor_23_out, notconnected_7_out[5], and_51_out);
  and and_51 (and_51_out, and_52_out, notconnected_7_out[4]);
  xor xor_24 (xor_24_out, notconnected_7_out[4], and_52_out);
  and and_52 (and_52_out, and_53_out, notconnected_7_out[3]);
  xor xor_25 (xor_25_out, notconnected_7_out[3], and_53_out);
  and and_53 (and_53_out, and_54_out, notconnected_7_out[2]);
  xor xor_26 (xor_26_out, notconnected_7_out[2], and_54_out);
  and and_54 (and_54_out, and_55_out, notconnected_7_out[1]);
  xor xor_27 (xor_27_out, notconnected_7_out[1], and_55_out);
  and and_55 (and_55_out, not_10_out, notconnected_7_out[0]);
  xor xor_28 (xor_28_out, notconnected_7_out[0], not_10_out);
  and and_56 (and_56_out, notconnected_8_out[4], notconnected_8_out[4]);
  or or_13 (or_13_out, notconnected_9_out[4], notconnected_9_out[4]);
  xor xor_29 (xor_29_out, notconnected_10_out[4], notconnected_10_out[4]);
  and and_57 (and_57_out, notconnected_8_out[5], notconnected_8_out[5]);
  or or_14 (or_14_out, notconnected_9_out[5], notconnected_9_out[5]);
  xor xor_30 (xor_30_out, notconnected_10_out[5], notconnected_10_out[5]);
  and and_58 (and_58_out, notconnected_8_out[6], notconnected_8_out[6]);
  and and_59 (and_59_out, notconnected_8_out[7], notconnected_8_out[7]);
  or or_15 (or_15_out, notconnected_9_out[6], notconnected_9_out[6]);
  or or_16 (or_16_out, notconnected_9_out[7], notconnected_9_out[7]);
  xor xor_31 (xor_31_out, notconnected_10_out[6], notconnected_10_out[6]);
  xor xor_32 (xor_32_out, notconnected_10_out[7], notconnected_10_out[7]);
  // NotConnected on notconnected_12_out
  // NotConnected on notconnected_13_out
  // NotConnected on notconnected_14_out
  and and_60 (and_60_out, notconnected_15_out, notconnected_12_out[0]);
  nand nand_1 (nand_1_out, notconnected_13_out[0], notconnected_13_out[0]);
  nor nor_19 (nor_19_out, notconnected_14_out[0], notconnected_14_out[0]);
  not not_11 (not_11_out, undriven_3);
  and and_61 (and_61_out, notconnected_15_out, notconnected_12_out[1]);
  and and_62 (and_62_out, notconnected_15_out, notconnected_12_out[2]);
  nand nand_2 (nand_2_out, notconnected_13_out[1], notconnected_13_out[1]);
  nand nand_3 (nand_3_out, notconnected_13_out[2], notconnected_13_out[2]);
  nor nor_20 (nor_20_out, notconnected_14_out[1], notconnected_14_out[1]);
  nor nor_21 (nor_21_out, notconnected_14_out[2], notconnected_14_out[2]);
  not not_12 (not_12_out, undriven_2);
  not not_13 (not_13_out, undriven);
  not not_14 (not_14_out, undriven_3);
  not not_15 (not_15_out, undriven_2);
  not not_16 (not_16_out, undriven);
  not not_17 (not_17_out, not_11_out);
  // NotConnected on notconnected_15_out
  and and_63 (and_63_out, notconnected_15_out, notconnected_12_out[3]);
  nand nand_4 (nand_4_out, notconnected_13_out[3], notconnected_13_out[3]);
  nor nor_22 (nor_22_out, notconnected_14_out[3], notconnected_14_out[3]);
  and and_64 (and_64_out, not_13_out, not_12_out);
  and and_65 (and_65_out, undriven, not_12_out);
  and and_66 (and_66_out, not_13_out, undriven_2);
  and and_67 (and_67_out, undriven_2, undriven);
  and and_68 (and_68_out, not_16_out, not_15_out);
  and and_69 (and_69_out, undriven, not_15_out);
  and and_70 (and_70_out, not_16_out, undriven_2);
  and and_71 (and_71_out, undriven_2, undriven);
  and and_72 (and_72_out, notconnected_15_out, notconnected_12_out[4]);
  nand nand_5 (nand_5_out, notconnected_13_out[4], notconnected_13_out[4]);
  nor nor_23 (nor_23_out, notconnected_14_out[4], notconnected_14_out[4]);
  and and_73 (and_73_out, and_64_out, not_14_out);
  and and_74 (and_74_out, and_65_out, not_14_out);
  and and_75 (and_75_out, and_66_out, not_14_out);
  and and_76 (and_76_out, and_67_out, not_14_out);
  and and_77 (and_77_out, and_68_out, not_17_out);
  and and_78 (and_78_out, and_69_out, not_17_out);
  and and_79 (and_79_out, and_70_out, not_17_out);
  and and_80 (and_80_out, and_71_out, not_17_out);
  and and_81 (and_81_out, notconnected_15_out, notconnected_12_out[5]);
  and and_82 (and_82_out, notconnected_15_out, notconnected_12_out[6]);
  nand nand_6 (nand_6_out, notconnected_13_out[5], notconnected_13_out[5]);
  nand nand_7 (nand_7_out, notconnected_13_out[6], notconnected_13_out[6]);
  nor nor_24 (nor_24_out, notconnected_14_out[5], notconnected_14_out[5]);
  nor nor_25 (nor_25_out, notconnected_14_out[6], notconnected_14_out[6]);
  and and_83 (and_83_out, notconnected_15_out, notconnected_12_out[7]);
  nand nand_8 (nand_8_out, notconnected_13_out[7], notconnected_13_out[7]);
  nor nor_26 (nor_26_out, notconnected_14_out[7], notconnected_14_out[7]);

  // Notes on the sheet:
  //   Register
  //   Save
  //   Load
  //   Save Value
  //   ADDER
  //   1 Bit mem
  //   SaveVal
  //   .
  //   Reset
  //   Write
  //   Always OUT
  //   OUT
  //   Always On Out
  //   Out
  //   AND
  //   OR
  //   XOR
  //   INCRMNT
  //   SWITCH
  //   NAND
  //   NOR
  //   3x8 Demux
  //   A1
  //   A2
  //   A3
  //   A_0
  //   2x4 Demux
  //   A_1
  //   Disable
endmodule
